# Fritzing sketch Untitled Sketch 9 (saved by Fritzing 0.9.3b)
breadboards: 1

parts:
  VCC1 = Battery block 9V
  S1 = Momentary Switch [package=ksa_sealed_tac_switch]
  R1 = Resistor [tolerance=±5% resistance=220 package=THT]
  LED1 = LED - 5mm [color="Red (633nm)" package="5 mm [THT]"]
  J1 = Piezo Speaker
  Q1 = TRANSISTOR_NPN [package=to-92-ammo]
  R2 = Resistor [tolerance=±5% resistance=220 package="1206 [SMD]"]
  PIR1 = PIR sensor

nets:
  N1: VCC1.-, Q1.B, R2.Pin_0, PIR1.GND
  N2: VCC1.+, S1.3
  N3: S1.2, R1.Pin_1, J1.pin2
  N4: R1.Pin_0, LED1.anode
  N5: J1.pin1, Q1.E
  N6: R2.Pin_1, PIR1.SIG
